# Fritzing sketch New_board4 (saved by Fritzing 0.9.3b)
circuit board: 12.2406cm x 7.35526cm
breadboards: 1

parts:
  U1 = V_REG_LD1117VXX [package=78xxl]
  C1 = Ceramic Capacitor [capacitance=100nF voltage=5.5V package="100 mil [THT, multilayer]"]
  C2 = Electrolytic Capacitor [capacitance=10µF package="100 mil [THT, electrolytic]"]
  S1 = Pushbutton [package="[THT]"]
  S2 = Pushbutton [package="[THT]"]
  S3 = Pushbutton [package="[THT]"]
  S4 = Pushbutton [package="[THT]"]
  S5 = Pushbutton [package="[THT]"]
  S6 = Toggle Switch [package=THT]
  S7 = Toggle Switch [package=THT]
  LED1 = LED - 5mm [color="Red (635nm)" package="5 mm [THT]"]
  LED2 = LED - 5mm [color="Yellow (585nm)" package="5 mm [THT]"]
  LED3 = LED - 5mm [color="Green (565nm)" package="5 mm [THT]"]
  LED4 = LED - 5mm [color="Blue (430nm)" package="5 mm [THT]"]
  R1 = Resistor [tolerance=±5% resistance=35 package=THT]
  R2 = Resistor [tolerance=±5% resistance=25 package=THT]
  R3 = Resistor [tolerance=±5% resistance=35 package=THT]
  R4 = Resistor [tolerance=±5% resistance=85 package=THT]
  J1 = Raspberry PI B 40-pin header [form="♂ (shrouded male)" package=THT]
  R21 = Resistor [tolerance=±5% resistance=2.2k package=THT]
  Q1 = NPN-Transistor [package="TO92 [THT]"]
  IC1 = Hex Inverter Schmitt Trigger SN74HC14 [package="DIP (Dual Inline)"]
  R1_2 = Resistor [tolerance=±5% resistance=47k package=THT]
  D1 = Rectifier Diode [part_number=1N4001 package="300 mil [THT]"]
  R2_2 = Resistor [tolerance=±5% resistance=47k package=THT]
  C3 = Electrolytic Capacitor [capacitance=1µF package="100 mil [THT, electrolytic]"]
  R23 = Resistor [tolerance=±5% resistance=47k package=THT]
  R24 = Resistor [tolerance=±5% resistance=47k package=THT]
  D2 = Rectifier Diode [part_number=1N4001 package="300 mil [THT]"]
  C4 = Electrolytic Capacitor [capacitance=1µF package="100 mil [THT, electrolytic]"]
  R25 = Resistor [tolerance=±5% resistance=47k package=THT]
  R26 = Resistor [tolerance=±5% resistance=47k package=THT]
  D3 = Rectifier Diode [part_number=1N4001 package="300 mil [THT]"]
  C5 = Electrolytic Capacitor [capacitance=1µF package="100 mil [THT, electrolytic]"]
  R27 = Resistor [tolerance=±5% resistance=47k package=THT]
  R28 = Resistor [tolerance=±5% resistance=47k package=THT]
  D4 = Rectifier Diode [part_number=1N4001 package="300 mil [THT]"]
  C6 = Electrolytic Capacitor [capacitance=1µF package="100 mil [THT, electrolytic]"]
  R29 = Resistor [tolerance=±5% resistance=47k package=THT]
  R30 = Resistor [tolerance=±5% resistance=47k package=THT]
  D5 = Rectifier Diode [part_number=1N4001 package="300 mil [THT]"]
  C7 = Electrolytic Capacitor [capacitance=1µF package="100 mil [THT, electrolytic]"]
  R35 = Resistor [tolerance=±5% resistance=150k package=THT]
  R38 = Resistor [tolerance=±5% resistance=2.2k package=THT]
  Q3 = NPN-Transistor [package="TO92 [THT]"]
  R40 = Resistor [tolerance=±5% resistance=2.2k package=THT]
  Q4 = NPN-Transistor [package="TO92 [THT]"]
  R42 = Resistor [tolerance=±5% resistance=2.2k package=THT]
  Q5 = NPN-Transistor [package="TO92 [THT]"]
  7_Segment1 = 7 Segment Display
  IC3 = IC, DIP package, 16 pins [chip_label=IC]
  R49 = Resistor [tolerance=±5% resistance=220k package=THT]
  R50 = Resistor [tolerance=±5% resistance=220k package=THT]
  R52 = Resistor [tolerance=±5% resistance=220k package=THT]
  R51 = Resistor [tolerance=±5% resistance=220k package=THT]
  R53 = Resistor [tolerance=±5% resistance=150k package=THT]
  IC7 = 4011 4 x 2 Input NAND Gate, single part [part_number=4011 package="DIP (Dual Inline) [THT]"]
  R55 = Resistor [tolerance=±5% resistance=150k package=THT]
  JP1 = Header 3 [package=jst-3-pth]
  JP2 = Header 2 [package=jst-2-pth]
  Part1 = Adafruit ADS1115 16Bit I2C ADC [part_number="Adafruit #1085"]

nets:
  N1: U1.OUT, C2.+, LED1.anode, LED2.anode, LED3.anode, R1_2.Pin_1, R23.Pin_1, R26.Pin_1, R28.Pin_1, R30.Pin_1, R35.Pin_1, R49.Pin_1, R50.Pin_1, R52.Pin_1, R51.Pin_1, R53.Pin_1, R55.Pin_1
  GND: U1.GND, C1.0, C2.-, S1.Pin_3, S1.Pin_4, S2.Pin_3, S2.Pin_4, S3.Pin_3, S3.Pin_4, S4.Pin_3, S4.Pin_4, S5.Pin_3, S5.Pin_4, S6.COM, S7.COM, J1.Pin_25, J1.Pin_39, J1.Pin_30, J1.Pin_20, J1.Pin_14, J1.Pin_6, Q1.E, IC1.GND, IC1.6A, C3.-, C4.-, C5.-, C6.-, C7.-, Q3.E, Q4.E, Q5.E, 7_Segment1.common_cathode, IC3.pin5, IC3.pin8, IC7.GND, JP1.3, Part1.GND
  N2: U1.IN, C1.1, LED4.anode, J1.Pin_4, J1.Pin_2
  N3: S1.Pin_1, S1.Pin_2, IC1.1A, R1_2.Pin_0, D1.anode, R2_2.Pin_1
  N4: S2.Pin_1, S2.Pin_2, IC1.2A, R23.Pin_0, R24.Pin_1, D2.anode
  N5: S3.Pin_1, S3.Pin_2, IC1.3A, R25.Pin_1, R26.Pin_0, D3.anode
  N6: S4.Pin_1, S4.Pin_2, IC1.4A, R27.Pin_1, R28.Pin_0, D4.anode
  N7: S5.Pin_1, S5.Pin_2, IC1.5A, R29.Pin_1, R30.Pin_0, D5.anode
  N8: S6.L1, R49.Pin_0, IC7.B1
  N9: S6.L2, R50.Pin_0, IC7.B2
  N10: S7.L1, R51.Pin_0, IC7.B4
  N11: S7.L2, R52.Pin_0, IC7.A3
  N12: LED1.cathode, R1.Pin_1
  N13: LED2.cathode, R2.Pin_1
  N14: LED3.cathode, R3.Pin_1
  N15: LED4.cathode, R4.Pin_1
  N16: R1.Pin_0, Q1.C
  N17: R2.Pin_0, Q3.C
  N18: R3.Pin_0, Q4.C
  N19: R4.Pin_0, Q5.C
  N20: J1.Pin_3, JP2.1
  N21: J1.Pin_5, JP2.2
  N22: J1.Pin_7, IC1.1Y
  N23: J1.Pin_19, IC7.B3, IC7.Q4
  N24: J1.Pin_21, IC7.A1, IC7.Q2
  N25: J1.Pin_23, R21.Pin_0
  N26: J1.Pin_29, IC1.2Y
  N27: J1.Pin_31, IC1.3Y
  N28: J1.Pin_33, R40.Pin_0
  N29: J1.Pin_32, R38.Pin_0
  N30: J1.Pin_26, IC1.4Y
  N31: J1.Pin_24, IC1.5Y
  N32: J1.Pin_10, JP1.2
  N33: J1.Pin_8, JP1.1
  N34: R21.Pin_1, Q1.B
  N35: IC1.VCC, R35.Pin_0
  N36: D1.cathode, R2_2.Pin_0, C3.+
  N37: R24.Pin_0, D2.cathode, C4.+
  N38: R25.Pin_0, D3.cathode, C5.+
  N39: R27.Pin_0, D4.cathode, C6.+
  N40: R29.Pin_0, D5.cathode, C7.+
  N41: R38.Pin_1, Q3.B
  N42: R40.Pin_1, Q4.B
  N43: R42.Pin_1, Q5.B
  N44: 7_Segment1.Segment_E, IC3.pin9
  N45: 7_Segment1.Segment_D, IC3.pin10
  N46: 7_Segment1.Segment_C, IC3.pin11
  N47: 7_Segment1.Segment_B, IC3.pin12
  N48: 7_Segment1.Segment_A, IC3.pin13
  N49: 7_Segment1.Segment_F, IC3.pin15
  N50: 7_Segment1.Segment_G, IC3.pin14
  N51: IC3.pin3, IC3.pin16, R55.Pin_0
  N52: R53.Pin_0, IC7.VDD
  N53: IC7.Q1, IC7.A2
  N54: IC7.Q3, IC7.A4

notes:
  800mA out
  make pullup/down external?
  3.3V 50mA is shared amongst ALL pins
  Blue LED needs 5V!
  RC debounce ROUGHLY
  C = 1uF
  R1+R2 = 80K
  delay time ~ 24ms
  at 3.3V
  with diode 35975
  feed trigger 74HC14
  ?????
  Resistors!
  Need to get measurements
  Tie GPCLK0 to the red LED as well? Speaker? TOGGLE SWITCH???
  remove v-divider(?)
  I2C
  UART

custom parts:
  Raspberry PI B 40-pin header: 40-pin header for the PI 3 model B
  Adafruit ADS1115 16Bit I2C ADC: For microcontrollers without an analog-to-digital converter or when you want a higher-precision ADC, the ADS1115 provides 16-bit precision at 860 samples/second over I2C. The chip can be configured as 4 single-ended input channels, or two differential channels. As a nice bonus, it even includes a programmable gain amplifier, up to x16, to help boost up smaller single/differential signals to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
